// Logisim project control-logic.circ as structural Verilog: 1 circuit, main circuit control_logic
module control_logic (
  input  [31:0] Instruction,
  input  BrEq,
  input  BrLt,
  output PCSel,
  output RegWEn,
  output [2:0] ImmSel,
  output BrUn,
  output ASel,
  output BSel,
  output [3:0] ALUSel,
  output MemWEn,
  output [1:0] WBSel
);

  wire add, add_mul_sub, addi, and_11_out, and_12_out, and_13_out, and_14_out, and_15_out, and_16_out,
       and_17_out, and_18_out, and_34_out, and_r, andi, auipc, B_Type, beq, bge, bgeu, blt, bltu, bne,
       comparator_9_eq, comparator_10_eq, comparator_11_eq, comparator_11_lt, comparator_12_eq,
       comparator_13_eq, comparator_14_eq, comparator_15_eq, comparator_16_eq, comparator_17_eq,
       comparator_18_eq, comparator_19_eq, comparator_20_eq, comparator_21_eq, comparator_21_lt,
       comparator_22_eq, comparator_23_eq, comparator_23_lt, comparator_24_eq, comparator_25_eq,
       comparator_26_eq, comparator_27_eq, comparator_28_eq, comparator_28_lt, comparator_29_eq,
       comparator_30_eq, comparator_31_eq, comparator_32_eq, comparator_33_eq, comparator_34_eq,
       comparator_35_eq, comparator_36_eq, comparator_37_eq, comparator_38_eq, comparator_39_eq,
       comparator_40_eq, comparator_41_eq, comparator_42_eq, I_Type, jal, jalr, lb, lh, load_Type, lui, lw,
       mul, mulh, mulhu, multiplexer_1_out, not_1_out, not_2_out, not_3_out, or_1_out, or_2_out, or_3_out,
       or_r, ori, R_Type, S_Type, sb, sh, sll_mulh, sll_r, slli, slt, slti, sr_i, sra_r, srai, srl_r,
       srl_sra, srli, sub, sw, xor_r, xori;
  wire [5:0] pri;
  wire [15:14] rom_1_data;

  Comparator #(.width(7)) comparator_1 (.a(Instruction[6:0]), .b(7'b0010011), .eq(I_Type));  // open: gt, lt
  Comparator #(.width(7)) comparator_2 (.a(Instruction[6:0]), .b(7'b0110011), .eq(R_Type));  // open: gt, lt
  Comparator #(.width(7)) comparator_3 (.a(Instruction[6:0]), .b(7'b1100011), .eq(B_Type));  // open: gt, lt
  Comparator #(.width(7)) comparator_4 (.a(Instruction[6:0]), .b(7'b0100011), .eq(S_Type));  // open: gt, lt
  Comparator #(.width(7)) comparator_5 (.a(Instruction[6:0]), .b(7'b0000011), .eq(load_Type));  // open: gt, lt
  Comparator #(.width(7)) comparator_6 (.a(Instruction[6:0]), .b(7'b0010111), .eq(auipc));  // open: gt, lt
  Comparator #(.width(7)) comparator_7 (.a(Instruction[6:0]), .b(7'b0110111), .eq(lui));  // open: gt, lt
  Comparator #(.width(7)) comparator_8 (.a(Instruction[6:0]), .b(7'b1101111), .eq(jal));  // open: gt, lt
  Comparator #(.width(7)) comparator_9 (.a(Instruction[6:0]), .b(7'b1100111), .eq(comparator_9_eq));  // open: gt, lt
  Comparator #(.width(3)) comparator_10 (.a(Instruction[14:12]), .b(3'b000), .eq(comparator_10_eq));  // open: gt, lt
  and and_1 (jalr, comparator_9_eq, comparator_10_eq);
  ROM #(.addrWidth(6), .dataWidth(16)) rom_1 (
    .addr(pri), .data({rom_1_data, WBSel, MemWEn, ALUSel, BSel, ASel, BrUn, ImmSel, RegWEn}));
  Priority_Encoder #(.select_enc(6)) priority_encoder_1 (
    .in0(add), .in1(mul), .in2(sub), .in3(sll_r), .in4(mulh), .in5(mulhu), .in6(slt), .in7(xor_r),
    .in8(srl_r), .in9(sra_r), .in10(or_r), .in11(and_r), .in12(lb), .in13(lh), .in14(lw), .in15(addi),
    .in16(slli), .in17(slti), .in18(xori), .in19(srli), .in20(srai), .in21(ori), .in22(andi), .in23(sb),
    .in24(sh), .in25(sw), .in26(beq), .in27(bne), .in28(blt), .in29(bge), .in30(bltu), .in31(bgeu),
    .in32(auipc), .in33(lui), .in34(jal), .in35(jalr), .out(pri));  // open: in36, in37, in38, in39, in40, in41, in42, in43, in44, in45, in46, in47, in48, in49, in50, in51, in52, in53, in54, in55, in56, in57, in58, in59, in60, in61, in62, in63, gs, en_out, en_in
  Comparator #(.width(7)) comparator_11 (
    .a(Instruction[31:25]), .b(7'b0100000), .eq(comparator_11_eq), .lt(comparator_11_lt));  // open: gt
  Comparator #(.width(3)) comparator_12 (.a(Instruction[14:12]), .b(3'b000), .eq(comparator_12_eq));  // open: gt, lt
  Comparator #(.width(3)) comparator_13 (.a(Instruction[14:12]), .b(3'b001), .eq(comparator_13_eq));  // open: gt, lt
  Comparator #(.width(3)) comparator_14 (.a(Instruction[14:12]), .b(3'b010), .eq(comparator_14_eq));  // open: gt, lt
  Comparator #(.width(3)) comparator_15 (.a(Instruction[14:12]), .b(3'b100), .eq(comparator_15_eq));  // open: gt, lt
  Comparator #(.width(3)) comparator_16 (.a(Instruction[14:12]), .b(3'b101), .eq(comparator_16_eq));  // open: gt, lt
  Comparator #(.width(3)) comparator_17 (.a(Instruction[14:12]), .b(3'b110), .eq(comparator_17_eq));  // open: gt, lt
  Comparator #(.width(3)) comparator_18 (.a(Instruction[14:12]), .b(3'b111), .eq(comparator_18_eq));  // open: gt, lt
  and and_2 (addi, I_Type, comparator_12_eq);
  and and_3 (slli, I_Type, comparator_13_eq);
  and and_4 (slti, I_Type, comparator_14_eq);
  and and_5 (xori, I_Type, comparator_15_eq);
  and and_6 (sr_i, I_Type, comparator_16_eq);
  and and_7 (srai, sr_i, comparator_11_eq);
  and and_8 (srli, comparator_11_lt, sr_i);
  and and_9 (ori, I_Type, comparator_17_eq);
  and and_10 (andi, I_Type, comparator_18_eq);
  not not_1 (not_1_out, BrEq);
  not not_2 (not_2_out, BrLt);
  not not_3 (not_3_out, BrLt);
  and and_11 (and_11_out, BrEq, beq);
  and and_12 (and_12_out, not_1_out, bne);
  and and_13 (and_13_out, BrLt, blt);
  and and_14 (and_14_out, not_2_out, bge);
  and and_15 (and_15_out, BrEq, bge);
  and and_16 (and_16_out, BrLt, bltu);
  and and_17 (and_17_out, not_3_out, bgeu);
  and and_18 (and_18_out, BrEq, bgeu);
  or or_1 (or_1_out, and_14_out, and_15_out);
  or or_2 (or_2_out, and_17_out, and_18_out);
  Comparator #(.width(3)) comparator_19 (.a(Instruction[14:12]), .b(3'b000), .eq(comparator_19_eq));  // open: gt, lt
  Comparator #(.width(7)) comparator_20 (
    .a(Instruction[31:25]), .b(7'b0100000), .eq(comparator_20_eq));  // open: gt, lt
  Comparator #(.width(7)) comparator_21 (
    .a(Instruction[31:25]), .b(7'b0000001), .eq(comparator_21_eq), .lt(comparator_21_lt));  // open: gt
  Comparator #(.width(3)) comparator_22 (.a(Instruction[14:12]), .b(3'b001), .eq(comparator_22_eq));  // open: gt, lt
  Comparator #(.width(7)) comparator_23 (
    .a(Instruction[31:25]), .b(7'b0000001), .eq(comparator_23_eq), .lt(comparator_23_lt));  // open: gt
  Comparator #(.width(3)) comparator_24 (.a(Instruction[14:12]), .b(3'b011), .eq(comparator_24_eq));  // open: gt, lt
  Comparator #(.width(3)) comparator_25 (.a(Instruction[14:12]), .b(3'b010), .eq(comparator_25_eq));  // open: gt, lt
  Comparator #(.width(3)) comparator_26 (.a(Instruction[14:12]), .b(3'b100), .eq(comparator_26_eq));  // open: gt, lt
  Comparator #(.width(3)) comparator_27 (.a(Instruction[14:12]), .b(3'b101), .eq(comparator_27_eq));  // open: gt, lt
  Comparator #(.width(7)) comparator_28 (
    .a(Instruction[31:25]), .b(7'b0100000), .eq(comparator_28_eq), .lt(comparator_28_lt));  // open: gt
  Comparator #(.width(3)) comparator_29 (.a(Instruction[14:12]), .b(3'b110), .eq(comparator_29_eq));  // open: gt, lt
  Comparator #(.width(3)) comparator_30 (.a(Instruction[14:12]), .b(3'b111), .eq(comparator_30_eq));  // open: gt, lt
  and and_19 (add_mul_sub, R_Type, comparator_19_eq);
  and and_20 (sll_mulh, R_Type, comparator_22_eq);
  and and_21 (mulhu, R_Type, comparator_24_eq);
  and and_22 (slt, R_Type, comparator_25_eq);
  and and_23 (xor_r, R_Type, comparator_26_eq);
  and and_24 (srl_sra, R_Type, comparator_27_eq);
  and and_25 (or_r, R_Type, comparator_29_eq);
  and and_26 (and_r, R_Type, comparator_30_eq);
  and and_27 (sub, add_mul_sub, comparator_20_eq);
  and and_28 (mul, add_mul_sub, comparator_21_eq);
  and and_29 (add, comparator_21_lt, add_mul_sub);
  and and_30 (mulh, sll_mulh, comparator_23_eq);
  and and_31 (sll_r, comparator_23_lt, sll_mulh);
  and and_32 (sra_r, srl_sra, comparator_28_eq);
  and and_33 (srl_r, comparator_28_lt, srl_sra);
  Multiplexer #(.select(3)) multiplexer_1 (
    .in0(and_11_out), .in1(and_12_out), .in4(and_13_out), .in5(or_1_out), .in6(and_16_out), .in7(or_2_out),
    .out(multiplexer_1_out), .sel(Instruction[14:12]));  // open: in2, in3
  and and_34 (and_34_out, B_Type, multiplexer_1_out);
  or or_3 (or_3_out, jal, jalr);
  Comparator #(.width(3)) comparator_31 (.a(Instruction[14:12]), .b(3'b000), .eq(comparator_31_eq));  // open: gt, lt
  Comparator #(.width(3)) comparator_32 (.a(Instruction[14:12]), .b(3'b001), .eq(comparator_32_eq));  // open: gt, lt
  Comparator #(.width(3)) comparator_33 (.a(Instruction[14:12]), .b(3'b100), .eq(comparator_33_eq));  // open: gt, lt
  Comparator #(.width(3)) comparator_34 (.a(Instruction[14:12]), .b(3'b101), .eq(comparator_34_eq));  // open: gt, lt
  Comparator #(.width(3)) comparator_35 (.a(Instruction[14:12]), .b(3'b110), .eq(comparator_35_eq));  // open: gt, lt
  Comparator #(.width(3)) comparator_36 (.a(Instruction[14:12]), .b(3'b111), .eq(comparator_36_eq));  // open: gt, lt
  and and_35 (beq, B_Type, comparator_31_eq);
  and and_36 (bne, B_Type, comparator_32_eq);
  and and_37 (blt, B_Type, comparator_33_eq);
  and and_38 (bge, B_Type, comparator_34_eq);
  and and_39 (bltu, B_Type, comparator_35_eq);
  and and_40 (bgeu, B_Type, comparator_36_eq);
  or or_4 (PCSel, or_3_out, and_34_out);
  Comparator #(.width(3)) comparator_37 (.a(Instruction[14:12]), .b(3'b000), .eq(comparator_37_eq));  // open: gt, lt
  Comparator #(.width(3)) comparator_38 (.a(Instruction[14:12]), .b(3'b001), .eq(comparator_38_eq));  // open: gt, lt
  Comparator #(.width(3)) comparator_39 (.a(Instruction[14:12]), .b(3'b010), .eq(comparator_39_eq));  // open: gt, lt
  Comparator #(.width(3)) comparator_40 (.a(Instruction[14:12]), .b(3'b000), .eq(comparator_40_eq));  // open: gt, lt
  Comparator #(.width(3)) comparator_41 (.a(Instruction[14:12]), .b(3'b001), .eq(comparator_41_eq));  // open: gt, lt
  Comparator #(.width(3)) comparator_42 (.a(Instruction[14:12]), .b(3'b010), .eq(comparator_42_eq));  // open: gt, lt
  and and_41 (sb, S_Type, comparator_37_eq);
  and and_42 (sh, S_Type, comparator_38_eq);
  and and_43 (sw, S_Type, comparator_39_eq);
  and and_44 (lb, load_Type, comparator_40_eq);
  and and_45 (lh, load_Type, comparator_41_eq);
  and and_46 (lw, load_Type, comparator_42_eq);

  // Other names for the same wires on the sheet: Opcode[6:0] = Instruction[6:0]; Funct3[2:0] = Instruction[14:12];
  //   Funct7[6:0] = Instruction[31:25]

  // Notes on the sheet:
  //   INPUTS to your circuit
  //   contents of rom_1 (hex, n*v repeats v):
  //   1001 1401 1601 1081 1481 1581 1101 1201 1281 1681 1301 1381 41 41 41 1041 10c1 1141 1241 12c1 16c1
  //   1341 13c1 842 842 842 4*1064 1074 1074 1067 17c7 2069 2041
  //   ROM FOR CONTROL LOGIC
  //   DON'T CHANGE THE LOCATIONS OF THE INPUTS AND OUTPUTS!
  //   This is only if you choose to do the ROM option
  //   OUTPUT from your circuit
  //   Reminder: If using ROM, use combinational logic for PCSel
endmodule
